// Logisim project CPU.circ as structural Verilog: 14 circuits, main circuit main
module main (
);

  wire alu_1_zf, clock_1_out, cu_1_acc, cu_1_acc_src, cu_1_ir, cu_1_mar, cu_1_mar_src, cu_1_mdr, cu_1_nload,
       cu_1_outp, cu_1_pc, cu_1_ram_out_en, cu_1_ram_wr_en, cu_1_tmp;
  wire [2:0] cu_1_alu;
  wire [7:0] ACC_q, alu_1_o, IR_q, MAR_q, MDR_q, mux2x8b_1_o, mux2x8b_2_o, OUTP_q, pc_1_addr, ram_1_dout,
       SW_sw8, TMP_q;

  Clock clock_1 (.out(clock_1_out));
  CU cu_1 (
    .CLK(clock_1_out), .nRST(1'b1), .OPCODE(IR_q), .ZF(alu_1_zf), .IR(cu_1_ir), .RAM_OUT_EN(cu_1_ram_out_en),
    .PC(cu_1_pc), .ACC(cu_1_acc), .nLOAD(cu_1_nload), .OUTP(cu_1_outp), .TMP(cu_1_tmp),
    .RAM_WR_EN(cu_1_ram_wr_en), .MDR(cu_1_mdr), .MAR(cu_1_mar), .MAR_SRC(cu_1_mar_src),
    .ACC_SRC(cu_1_acc_src), .ALU(cu_1_alu));  // open: nCLK_EN
  DipSwitch SW (
    .sw1(SW_sw8[7]), .sw2(SW_sw8[6]), .sw3(SW_sw8[5]), .sw4(SW_sw8[4]), .sw5(SW_sw8[3]), .sw6(SW_sw8[2]),
    .sw7(SW_sw8[1]), .sw8(SW_sw8[0]));
  PC pc_1 (.nRESET(1'b1), .CLK(cu_1_pc), .SET(alu_1_o), .nLOAD(cu_1_nload), .ADDR(pc_1_addr));
  REG8b IR (.nRESET(1'b1), .D(alu_1_o), .CLK(cu_1_ir), .Q(IR_q));
  MUX2x8b mux2x8b_1 (.S0(cu_1_acc_src), .A(alu_1_o), .B(SW_sw8), .O(mux2x8b_1_o));
  MUX2x8b mux2x8b_2 (.S0(cu_1_mar_src), .A(pc_1_addr), .B(alu_1_o), .O(mux2x8b_2_o));
  REG8b ACC (.nRESET(1'b1), .D(mux2x8b_1_o), .CLK(cu_1_acc), .Q(ACC_q));
  REG8b TMP (.nRESET(1'b1), .D(alu_1_o), .CLK(cu_1_tmp), .Q(TMP_q));
  REG8b MAR (.nRESET(1'b1), .D(mux2x8b_2_o), .CLK(cu_1_mar), .Q(MAR_q));
  REG8b MDR (.nRESET(1'b1), .D(alu_1_o), .CLK(cu_1_mdr), .Q(MDR_q));
  RAM #(.addrWidth(13)) ram_1 (
    .addr({{5{1'b0}}, MAR_q}), .we(cu_1_ram_wr_en), .oe(cu_1_ram_out_en), .clk(clock_1_out), .din(MDR_q),
    .dout(ram_1_dout));
  ALU alu_1 (.S(cu_1_alu), .A(ACC_q), .B(TMP_q), .O(alu_1_o), .ZF(alu_1_zf));  // open: CF
  assign alu_1_o = cu_1_ram_out_en ? ram_1_dout : 8'bz;  // Controlled_Buffer controlled_buffer_1
  REG8b OUTP (.nRESET(1'b1), .D(alu_1_o), .CLK(cu_1_outp), .Q(OUTP_q));
  LED led_1 (.in(OUTP_q[7]));
  LED led_2 (.in(OUTP_q[6]));
  LED led_3 (.in(OUTP_q[5]));
  LED led_4 (.in(OUTP_q[4]));
  LED led_5 (.in(OUTP_q[3]));
  LED led_6 (.in(OUTP_q[2]));
  LED led_7 (.in(OUTP_q[1]));
  LED led_8 (.in(OUTP_q[0]));

  // Notes on the sheet:
  //   DATA
  //   ADDR
endmodule

module ALU (
  input  [2:0] S,
  input  [7:0] A,
  input  [7:0] B,
  output [7:0] O,
  output CF,
  output ZF
);

  wire n7402_1_pin1, n7402_1_pin4, n7402_1_pin10, n7402_1_pin13, n7408_1_pin3, n7408_1_pin6, n74138_1_pin4,
       n74138_1_pin6, n74138_1_pin10, n74138_1_pin11, n74138_1_pin12, n74138_1_pin13, n74138_1_pin14,
       n74138_1_pin15, n74244_2_pin1;
  wire [7:0] add_1_z, and8b_1_z, invert_1_z;

  _74138 #(.ShowInternalStructure("true")) u_74138_1 (
    .pin1(S[0]), .pin2(S[1]), .pin3(S[2]), .pin4(n74138_1_pin4), .pin5(n74138_1_pin4), .pin6(n74138_1_pin6),
    .pin15(n74138_1_pin15), .pin14(n74138_1_pin14), .pin13(n74138_1_pin13), .pin12(n74138_1_pin12),
    .pin11(n74138_1_pin11), .pin10(n74138_1_pin10));  // open: pin7, pin9
  // NoConnect on n74138_1_pin15
  INVERT invert_1 (.EN(n74138_1_pin13), .X(B), .Z(invert_1_z));
  ADD add_1 (.X(A), .Y(invert_1_z), .CIN(n74138_1_pin13), .Z(add_1_z), .CF(CF));
  AND8b and8b_1 (.A(A), .B(B), .Z(and8b_1_z));
  _74244 #(.ShowInternalStructure("true")) u_74244_1 (
    .pin1(n74138_1_pin14), .pin2(A[7]), .pin3(O[0]), .pin4(A[6]), .pin5(O[1]), .pin6(A[5]), .pin7(O[2]),
    .pin8(A[4]), .pin9(O[3]), .pin19(n74138_1_pin14), .pin18(O[7]), .pin17(A[0]), .pin16(O[6]), .pin15(A[1]),
    .pin14(O[5]), .pin13(A[2]), .pin12(O[4]), .pin11(A[3]));
  _74244 #(.ShowInternalStructure("true")) u_74244_2 (
    .pin1(n74244_2_pin1), .pin2(add_1_z[7]), .pin3(O[0]), .pin4(add_1_z[6]), .pin5(O[1]), .pin6(add_1_z[5]),
    .pin7(O[2]), .pin8(add_1_z[4]), .pin9(O[3]), .pin19(n74244_2_pin1), .pin18(O[7]), .pin17(add_1_z[0]),
    .pin16(O[6]), .pin15(add_1_z[1]), .pin14(O[5]), .pin13(add_1_z[2]), .pin12(O[4]), .pin11(add_1_z[3]));
  _74240 #(.ShowInternalStructure("true")) u_74240_1 (
    .pin1(n74138_1_pin11), .pin2(A[7]), .pin3(O[0]), .pin4(A[6]), .pin5(O[1]), .pin6(A[5]), .pin7(O[2]),
    .pin8(A[4]), .pin9(O[3]), .pin19(n74138_1_pin11), .pin18(O[7]), .pin17(A[0]), .pin16(O[6]), .pin15(A[1]),
    .pin14(O[5]), .pin13(A[2]), .pin12(O[4]), .pin11(A[3]));
  _74244 #(.ShowInternalStructure("true")) u_74244_3 (
    .pin1(n74138_1_pin10), .pin2(and8b_1_z[7]), .pin3(O[0]), .pin4(and8b_1_z[6]), .pin5(O[1]),
    .pin6(and8b_1_z[5]), .pin7(O[2]), .pin8(and8b_1_z[4]), .pin9(O[3]), .pin19(n74138_1_pin10), .pin18(O[7]),
    .pin17(and8b_1_z[0]), .pin16(O[6]), .pin15(and8b_1_z[1]), .pin14(O[5]), .pin13(and8b_1_z[2]),
    .pin12(O[4]), .pin11(and8b_1_z[3]));
  _7402 #(.ShowInternalStructure("true")) u_7402_1 (
    .pin1(n7402_1_pin1), .pin2(O[4]), .pin3(O[5]), .pin4(n7402_1_pin4), .pin5(O[6]), .pin6(O[7]),
    .pin13(n7402_1_pin13), .pin12(O[0]), .pin11(O[1]), .pin10(n7402_1_pin10), .pin9(O[2]), .pin8(O[3]));
  _7408 #(.ShowInternalStructure("true")) u_7408_1 (
    .pin1(n7402_1_pin13), .pin2(n7402_1_pin10), .pin3(n7408_1_pin3), .pin4(n7402_1_pin4),
    .pin5(n7402_1_pin1), .pin6(n7408_1_pin6), .pin13(n7408_1_pin3), .pin12(n7408_1_pin6), .pin11(ZF),
    .pin10(n74138_1_pin12), .pin9(n74138_1_pin13), .pin8(n74244_2_pin1));
  // also tied to GND on the sheet: n74138_1_pin4
  // also tied to VCC on the sheet: n74138_1_pin6

  // Notes on the sheet:
  //   0b000: disabled
  //   0b001: A
  //   0b010: A+B
  //   0b011: A-B
  //   0b100: ~A
  //   0b101: A&B
endmodule

module ADD (
  input  [7:0] X,
  input  [7:0] Y,
  input  CIN,
  output [7:0] Z,
  output CF
);

  wire n74283_1_pin7;

  _74283 #(.ShowInternalStructure("true")) u_74283_1 (
    .pin1(Z[5]), .pin2(Y[5]), .pin3(X[5]), .pin4(Z[4]), .pin5(X[4]), .pin6(Y[4]), .pin7(n74283_1_pin7),
    .pin15(Y[6]), .pin14(X[6]), .pin13(Z[6]), .pin12(X[7]), .pin11(Y[7]), .pin10(Z[7]), .pin9(CF));
  _74283 #(.ShowInternalStructure("true")) u_74283_2 (
    .pin1(Z[1]), .pin2(Y[1]), .pin3(X[1]), .pin4(Z[0]), .pin5(X[0]), .pin6(Y[0]), .pin7(CIN), .pin15(Y[2]),
    .pin14(X[2]), .pin13(Z[2]), .pin12(X[3]), .pin11(Y[3]), .pin10(Z[3]), .pin9(n74283_1_pin7));
endmodule

module INVERT (
  input  EN,
  input  [7:0] X,
  output [7:0] Z
);

  _7486 #(.ShowInternalStructure("true")) u_7486_1 (
    .pin1(EN), .pin2(X[4]), .pin3(Z[4]), .pin4(EN), .pin5(X[5]), .pin6(Z[5]), .pin13(EN), .pin12(X[7]),
    .pin11(Z[7]), .pin10(EN), .pin9(X[6]), .pin8(Z[6]));
  _7486 #(.ShowInternalStructure("true")) u_7486_2 (
    .pin1(EN), .pin2(X[0]), .pin3(Z[0]), .pin4(EN), .pin5(X[1]), .pin6(Z[1]), .pin13(EN), .pin12(X[3]),
    .pin11(Z[3]), .pin10(EN), .pin9(X[2]), .pin8(Z[2]));
endmodule

module PC (
  input  nRESET,
  input  CLK,
  input  [7:0] SET,
  input  nLOAD,
  output [7:0] ADDR
);

  wire n74163_1_pin7;

  _74163 #(.ShowInternalStructure("true")) u_74163_1 (
    .pin1(nRESET), .pin2(CLK), .pin3(SET[4]), .pin4(SET[5]), .pin5(SET[6]), .pin6(SET[7]),
    .pin7(n74163_1_pin7), .pin14(ADDR[4]), .pin13(ADDR[5]), .pin12(ADDR[6]), .pin11(ADDR[7]),
    .pin10(n74163_1_pin7), .pin9(nLOAD));  // open: pin15
  _74163 #(.ShowInternalStructure("true")) u_74163_2 (
    .pin1(nRESET), .pin2(CLK), .pin3(SET[0]), .pin4(SET[1]), .pin5(SET[2]), .pin6(SET[3]), .pin7(nRESET),
    .pin15(n74163_1_pin7), .pin14(ADDR[0]), .pin13(ADDR[1]), .pin12(ADDR[2]), .pin11(ADDR[3]),
    .pin10(nRESET), .pin9(nLOAD));
endmodule

module AND8b (
  input  [7:0] A,
  input  [7:0] B,
  output [7:0] Z
);

  _7408 #(.ShowInternalStructure("true")) u_7408_1 (
    .pin1(A[7]), .pin2(B[7]), .pin3(Z[7]), .pin4(A[6]), .pin5(B[6]), .pin6(Z[6]), .pin13(A[5]), .pin12(B[5]),
    .pin11(Z[5]), .pin10(A[4]), .pin9(B[4]), .pin8(Z[4]));
  _7408 #(.ShowInternalStructure("true")) u_7408_2 (
    .pin1(A[3]), .pin2(B[3]), .pin3(Z[3]), .pin4(A[2]), .pin5(B[2]), .pin6(Z[2]), .pin13(A[1]), .pin12(B[1]),
    .pin11(Z[1]), .pin10(A[0]), .pin9(B[0]), .pin8(Z[0]));
endmodule

module REG8b (
  input  nRESET,
  input  [7:0] D,
  input  CLK,
  output [7:0] Q
);

  _74273 #(.ShowInternalStructure("true")) u_74273_1 (
    .pin1(nRESET), .pin2(Q[0]), .pin3(D[0]), .pin4(D[1]), .pin5(Q[1]), .pin6(Q[2]), .pin7(D[2]), .pin8(D[3]),
    .pin9(Q[3]), .pin19(Q[7]), .pin18(D[7]), .pin17(D[6]), .pin16(Q[6]), .pin15(Q[5]), .pin14(D[5]),
    .pin13(D[4]), .pin12(Q[4]), .pin11(CLK));
endmodule

module MUX4x8b (
  input  S1,
  input  S0,
  input  [7:0] A,
  input  [7:0] B,
  input  [7:0] C,
  input  [7:0] D,
  output [7:0] O
);

  wire n74139_1_pin1, n74139_1_pin4, n74139_1_pin5, n74139_1_pin6, n74139_1_pin7;

  _74139 #(.ShowInternalStructure("true")) u_74139_1 (
    .pin1(n74139_1_pin1), .pin2(S1), .pin3(S0), .pin4(n74139_1_pin4), .pin5(n74139_1_pin5),
    .pin6(n74139_1_pin6), .pin7(n74139_1_pin7));  // open: pin15, pin14, pin13, pin12, pin11, pin10, pin9
  _74244 #(.ShowInternalStructure("true")) u_74244_1 (
    .pin1(n74139_1_pin4), .pin2(A[7]), .pin3(O[3]), .pin4(A[6]), .pin5(O[2]), .pin6(A[5]), .pin7(O[1]),
    .pin8(A[4]), .pin9(O[0]), .pin19(n74139_1_pin4), .pin18(O[7]), .pin17(A[3]), .pin16(O[6]), .pin15(A[2]),
    .pin14(O[5]), .pin13(A[1]), .pin12(O[4]), .pin11(A[0]));
  _74244 #(.ShowInternalStructure("true")) u_74244_2 (
    .pin1(n74139_1_pin5), .pin2(B[7]), .pin3(O[3]), .pin4(B[6]), .pin5(O[2]), .pin6(B[5]), .pin7(O[1]),
    .pin8(B[4]), .pin9(O[0]), .pin19(n74139_1_pin5), .pin18(O[7]), .pin17(B[3]), .pin16(O[6]), .pin15(B[2]),
    .pin14(O[5]), .pin13(B[1]), .pin12(O[4]), .pin11(B[0]));
  _74244 #(.ShowInternalStructure("true")) u_74244_3 (
    .pin1(n74139_1_pin6), .pin2(C[7]), .pin3(O[3]), .pin4(C[6]), .pin5(O[2]), .pin6(C[5]), .pin7(O[1]),
    .pin8(C[4]), .pin9(O[0]), .pin19(n74139_1_pin6), .pin18(O[7]), .pin17(C[3]), .pin16(O[6]), .pin15(C[2]),
    .pin14(O[5]), .pin13(C[1]), .pin12(O[4]), .pin11(C[0]));
  _74244 #(.ShowInternalStructure("true")) u_74244_4 (
    .pin1(n74139_1_pin7), .pin2(D[7]), .pin3(O[3]), .pin4(D[6]), .pin5(O[2]), .pin6(D[5]), .pin7(O[1]),
    .pin8(D[4]), .pin9(O[0]), .pin19(n74139_1_pin7), .pin18(O[7]), .pin17(D[3]), .pin16(O[6]), .pin15(D[2]),
    .pin14(O[5]), .pin13(D[1]), .pin12(O[4]), .pin11(D[0]));
  // also tied to GND on the sheet: n74139_1_pin1
endmodule

module MUX2x8b (
  input  S0,
  input  [7:0] A,
  input  [7:0] B,
  output [7:0] O
);

  _74241 #(.ShowInternalStructure("true")) u_74241_1 (
    .pin1(S0), .pin2(A[7]), .pin3(O[7]), .pin4(A[6]), .pin5(O[6]), .pin6(A[5]), .pin7(O[5]), .pin8(A[4]),
    .pin9(O[4]), .pin19(S0), .pin18(O[7]), .pin17(B[7]), .pin16(O[6]), .pin15(B[6]), .pin14(O[5]),
    .pin13(B[5]), .pin12(O[4]), .pin11(B[4]));
  _74241 #(.ShowInternalStructure("true")) u_74241_2 (
    .pin1(S0), .pin2(A[3]), .pin3(O[3]), .pin4(A[2]), .pin5(O[2]), .pin6(A[1]), .pin7(O[1]), .pin8(A[0]),
    .pin9(O[0]), .pin19(S0), .pin18(O[3]), .pin17(B[3]), .pin16(O[2]), .pin15(B[2]), .pin14(O[1]),
    .pin13(B[1]), .pin12(O[0]), .pin11(B[0]));
endmodule

module SEQ (
  input  CLK,
  input  nRST,
  output S0,
  output S1,
  output S2,
  output S3,
  output S4,
  output S5,
  output S6,
  output S7,
  output S8
);

  wire n7474_1_pin1;

  _7474 #(.ShowInternalStructure("true")) u_7474_1 (
    .pin1(n7474_1_pin1), .pin2(S8), .pin3(CLK), .pin4(nRST), .pin5(S0));  // open: pin6, pin13, pin12, pin11, pin10, pin9, pin8
  _74273 #(.ShowInternalStructure("true")) u_74273_1 (
    .pin1(nRST), .pin2(S1), .pin3(S0), .pin4(S1), .pin5(S2), .pin6(S3), .pin7(S2), .pin8(S3), .pin9(S4),
    .pin19(S8), .pin18(S7), .pin17(S6), .pin16(S7), .pin15(S6), .pin14(S5), .pin13(S4), .pin12(S5),
    .pin11(CLK));
  // also tied to VCC on the sheet: n7474_1_pin1
endmodule

module CU (
  input  CLK,
  input  nRST,
  input  [7:0] OPCODE,
  input  ZF,
  output IR,
  output RAM_OUT_EN,
  output PC,
  output ACC,
  output nLOAD,
  output OUTP,
  output TMP,
  output RAM_WR_EN,
  output MDR,
  output nCLK_EN,
  output MAR,
  output MAR_SRC,
  output ACC_SRC,
  output [2:0] ALU
);

  wire INC_PC, LOAD_PC, n7408_2_pin5, n7408_2_pin9, n7408_2_pin11, n7408_4_pin2, n7408_5_pin3, n7408_5_pin6,
       n7408_5_pin8, n7408_5_pin11, n7414_1_pin2, n7414_1_pin4, n7414_1_pin6, n7414_1_pin8, n7414_1_pin10,
       n7414_1_pin12, n7432_1_pin5, n7432_1_pin6, n7432_1_pin10, n7432_1_pin12, n7432_1_pin13, n7432_2_pin3,
       n7432_3_pin3, n7432_3_pin6, n7432_3_pin12, n74138_1_pin4, n74138_1_pin6, n74138_1_pin9,
       n74138_1_pin10, n74138_1_pin11, n74138_1_pin12, n74138_1_pin13, n74138_1_pin14, ram_latch_1_jnz,
       seq_1_s2, seq_1_s3, seq_1_s4, seq_1_s5, seq_1_s6, seq_1_s7, seq_1_s8;
  wire [2:0] n7408_2_pin6;

  SEQ seq_1 (
    .CLK(CLK), .nRST(nRST), .S0(n7408_2_pin6[2]), .S1(IR), .S2(seq_1_s2), .S3(seq_1_s3), .S4(seq_1_s4),
    .S5(seq_1_s5), .S6(seq_1_s6), .S7(seq_1_s7), .S8(seq_1_s8));
  _74138 #(.ShowInternalStructure("true")) u_74138_1 (
    .pin1(OPCODE[4]), .pin2(OPCODE[5]), .pin3(OPCODE[6]), .pin4(n74138_1_pin4), .pin5(n74138_1_pin4),
    .pin6(n74138_1_pin6), .pin14(n74138_1_pin14), .pin13(n74138_1_pin13), .pin12(n74138_1_pin12),
    .pin11(n74138_1_pin11), .pin10(n74138_1_pin10), .pin9(n74138_1_pin9));  // open: pin7, pin15
  _7414 #(.ShowInternalStructure("true")) u_7414_1 (
    .pin1(n74138_1_pin14), .pin2(n7414_1_pin2), .pin3(n74138_1_pin13), .pin4(n7414_1_pin4),
    .pin5(n74138_1_pin12), .pin6(n7414_1_pin6), .pin13(n74138_1_pin9), .pin12(n7414_1_pin12),
    .pin11(n74138_1_pin10), .pin10(n7414_1_pin10), .pin9(n74138_1_pin11), .pin8(n7414_1_pin8));
  _7432 #(.ShowInternalStructure("true")) u_7432_1 (
    .pin4(seq_1_s2), .pin5(n7432_1_pin5), .pin6(n7432_1_pin6), .pin13(n7432_1_pin13), .pin12(n7432_1_pin12),
    .pin11(LOAD_PC), .pin10(n7432_1_pin10), .pin9(n7432_1_pin6), .pin8(INC_PC));  // open: pin1, pin2, pin3
  _7408 #(.ShowInternalStructure("true")) u_7408_1 (
    .pin1(seq_1_s3), .pin2(OPCODE[3]), .pin3(TMP), .pin4(seq_1_s3), .pin5(n7414_1_pin8), .pin6(MDR),
    .pin13(seq_1_s8), .pin12(n7414_1_pin8), .pin11(RAM_WR_EN));  // open: pin10, pin9, pin8
  RAM_LATCH ram_latch_1 (
    .EN(n7408_2_pin6), .ZF(ZF), .DIS(seq_1_s2), .S5(seq_1_s5), .RAM_OUT_EN(RAM_OUT_EN), .JNZ(ram_latch_1_jnz));
  _7408 #(.ShowInternalStructure("true")) u_7408_2 (
    .pin1(seq_1_s3), .pin2(n7414_1_pin2), .pin3(n7432_1_pin13), .pin4(seq_1_s8), .pin5(n7408_2_pin5),
    .pin6(n7408_2_pin6[0]), .pin13(seq_1_s8), .pin12(n7414_1_pin2), .pin11(n7408_2_pin11), .pin10(seq_1_s5),
    .pin9(n7408_2_pin9), .pin8(n7408_2_pin6[0]));
  _7408 #(.ShowInternalStructure("true")) u_7408_3 (
    .pin1(seq_1_s7), .pin2(OPCODE[3]), .pin3(ACC), .pin4(seq_1_s7), .pin5(n7414_1_pin12), .pin6(OUTP),
    .pin13(seq_1_s7), .pin12(n7408_2_pin5), .pin11(n7432_1_pin12), .pin10(ZF), .pin9(n7414_1_pin4),
    .pin8(n7408_2_pin5));
  SRC_LATCH src_latch_1 (
    .S2(seq_1_s2), .S5(seq_1_s5), .iLOAD(n7414_1_pin6), .iIN(n7414_1_pin10), .S6(seq_1_s6),
    .iSTOR(n7414_1_pin8), .S8(seq_1_s8), .S1(IR), .MAR_SRC(MAR_SRC), .ACC_SRC(ACC_SRC));
  ALU_LATCH alu_latch_1 (.S5(seq_1_s5), .S0(n7408_2_pin6[2]), .S2(seq_1_s2), .Y(OPCODE[2:0]), .Z(ALU));
  _7408 #(.ShowInternalStructure("true")) u_7408_4 (
    .pin1(n7414_1_pin4), .pin2(n7408_4_pin2), .pin3(n7408_2_pin6[1]), .pin4(seq_1_s5), .pin5(ZF),
    .pin6(n7408_4_pin2), .pin13(ram_latch_1_jnz), .pin12(n7414_1_pin4), .pin11(n7432_1_pin5),
    .pin10(n7414_1_pin8), .pin9(seq_1_s5), .pin8(n7432_1_pin10));
  _7432 #(.ShowInternalStructure("true")) u_7432_2 (
    .pin1(n7408_2_pin11), .pin2(n7408_2_pin6[0]), .pin3(n7432_2_pin3), .pin13(LOAD_PC), .pin12(INC_PC),
    .pin11(PC), .pin10(n7414_1_pin8), .pin9(n7414_1_pin6), .pin8(n7408_2_pin9));  // open: pin4, pin5, pin6
  _7408 #(.ShowInternalStructure("true")) u_7408_5 (
    .pin1(seq_1_s7), .pin2(n7414_1_pin8), .pin3(n7408_5_pin3), .pin4(n7414_1_pin2), .pin5(seq_1_s4),
    .pin6(n7408_5_pin6), .pin13(n7414_1_pin2), .pin12(n7414_1_pin4), .pin11(n7408_5_pin11), .pin10(seq_1_s7),
    .pin9(n7414_1_pin6), .pin8(n7408_5_pin8));
  _7432 #(.ShowInternalStructure("true")) u_7432_3 (
    .pin1(n7408_5_pin3), .pin2(n7408_2_pin6[2]), .pin3(n7432_3_pin3), .pin4(n7408_5_pin6),
    .pin5(n7408_5_pin8), .pin6(n7432_3_pin6), .pin13(n7408_5_pin11), .pin12(n7432_3_pin12), .pin11(MAR),
    .pin10(n7432_3_pin3), .pin9(n7432_3_pin6), .pin8(n7432_3_pin12));
  _7414 #(.ShowInternalStructure("true")) u_7414_2 (
    .pin1(n7432_2_pin3), .pin2(nLOAD));  // open: pin3, pin4, pin5, pin6, pin13, pin12, pin11, pin10, pin9, pin8

  assign nCLK_EN = OPCODE[7];
  // also tied to GND on the sheet: n74138_1_pin4
  // also tied to VCC on the sheet: n74138_1_pin6
endmodule

module RAM_LATCH (
  input  [2:0] EN,
  input  ZF,
  input  DIS,
  input  S5,
  output RAM_OUT_EN,
  output JNZ
);

  wire n7404_1_pin2, n7404_1_pin4, n7404_1_pin10, n7404_1_pin12, n7432_1_pin3, n7432_1_pin6, n7474_1_pin2,
       n7474_1_pin12;

  _7432 #(.ShowInternalStructure("true")) u_7432_1 (
    .pin1(EN[0]), .pin2(EN[1]), .pin3(n7432_1_pin3), .pin4(EN[2]), .pin5(n7432_1_pin3), .pin6(n7432_1_pin6));  // open: pin13, pin12, pin11, pin10, pin9, pin8
  _7404 #(.ShowInternalStructure("true")) u_7404_1 (
    .pin1(n7432_1_pin6), .pin2(n7404_1_pin2), .pin3(DIS), .pin4(n7404_1_pin4), .pin13(ZF),
    .pin12(n7404_1_pin12), .pin11(S5), .pin10(n7404_1_pin10));  // open: pin5, pin6, pin9, pin8
  _7474 #(.ShowInternalStructure("true")) u_7474_1 (
    .pin1(n7404_1_pin4), .pin2(n7474_1_pin2), .pin3(n7474_1_pin2), .pin4(n7404_1_pin2), .pin5(RAM_OUT_EN),
    .pin13(n7404_1_pin10), .pin12(n7474_1_pin12), .pin11(n7474_1_pin12), .pin10(n7404_1_pin12), .pin9(JNZ));  // open: pin6, pin8
  // also tied to GND on the sheet: {n7474_1_pin2, n7474_1_pin12}
endmodule

module SRC_LATCH (
  input  S2,
  input  S5,
  input  iLOAD,
  input  iIN,
  input  S6,
  input  iSTOR,
  input  S8,
  input  S1,
  output MAR_SRC,
  output ACC_SRC
);

  wire n7404_1_pin2, n7404_1_pin4, n7404_1_pin10, n7404_1_pin12, n7458_1_pin1, n7458_1_pin6, n7458_1_pin8,
       n7458_1_pin11, n7474_1_pin2, n7474_1_pin12;

  _7458 #(.ShowInternalStructure("true")) u_7458_1 (
    .pin1(n7458_1_pin1), .pin2(S2), .pin3(iLOAD), .pin4(S6), .pin5(iSTOR), .pin6(n7458_1_pin6), .pin13(S5),
    .pin12(iIN), .pin11(n7458_1_pin11), .pin10(n7458_1_pin11), .pin9(n7458_1_pin11), .pin8(n7458_1_pin8));
  _7404 #(.ShowInternalStructure("true")) u_7404_1 (
    .pin1(n7458_1_pin6), .pin2(n7404_1_pin2), .pin3(S8), .pin4(n7404_1_pin4), .pin13(n7458_1_pin8),
    .pin12(n7404_1_pin12), .pin11(S1), .pin10(n7404_1_pin10));  // open: pin5, pin6, pin9, pin8
  _7474 #(.ShowInternalStructure("true")) u_7474_1 (
    .pin1(n7404_1_pin4), .pin2(n7474_1_pin2), .pin3(n7474_1_pin2), .pin4(n7404_1_pin2), .pin5(MAR_SRC),
    .pin13(n7404_1_pin10), .pin12(n7474_1_pin12), .pin11(n7474_1_pin12), .pin10(n7404_1_pin12), .pin9(ACC_SRC));  // open: pin6, pin8
  // also tied to GND on the sheet: {n7474_1_pin2, n7458_1_pin11, n7474_1_pin12}
  // also tied to VCC on the sheet: n7458_1_pin1
endmodule

module ALU_LATCH (
  input  S5,
  input  S0,
  input  S2,
  input  [2:0] Y,
  output [2:0] Z
);

  wire n7402_1_pin1, n7402_1_pin4, n7402_1_pin6, n7402_1_pin11, n7402_1_pin13, n74157_1_pin3, n74157_1_pin4,
       n74157_1_pin6, n74157_1_pin7, n74157_1_pin9, n74157_1_pin15;

  _74157 #(.ShowInternalStructure("true")) u_74157_1 (
    .pin1(S2), .pin2(Y[0]), .pin3(n74157_1_pin3), .pin4(n74157_1_pin4), .pin5(Y[1]), .pin6(n74157_1_pin6),
    .pin7(n74157_1_pin7), .pin15(n74157_1_pin15), .pin11(Y[2]), .pin10(n74157_1_pin15), .pin9(n74157_1_pin9));  // open: pin14, pin13, pin12
  _7402 #(.ShowInternalStructure("true")) u_7402_1 (
    .pin1(n7402_1_pin1), .pin2(S5), .pin3(S2), .pin4(n7402_1_pin4), .pin5(S0), .pin6(n7402_1_pin6),
    .pin13(n7402_1_pin13), .pin12(n7402_1_pin1), .pin11(n7402_1_pin11));  // open: pin10, pin9, pin8
  _74175 #(.ShowInternalStructure("true")) u_74175_1 (
    .pin1(n7402_1_pin4), .pin2(Z[0]), .pin4(n74157_1_pin4), .pin5(n74157_1_pin7), .pin7(Z[1]),
    .pin12(n74157_1_pin9), .pin10(Z[2]), .pin9(n7402_1_pin13));  // open: pin3, pin6, pin15, pin14, pin13, pin11
  // also tied to GND on the sheet: {n74157_1_pin6, n74157_1_pin15, n7402_1_pin6, n7402_1_pin11}
  // also tied to VCC on the sheet: n74157_1_pin3
endmodule
